# Fritzing sketch proof_of_concept_1DC_2stepper (saved by Fritzing 1.0.6)
breadboards: 1

parts:
  Part1 = Arduino Nano (Rev3.0)
  Moto1Driver = TMC2209 [package=THT]
  Moto2Driver = TMC2209 [package=THT]

nets:
  GND: Part1.GND, Moto1Driver.GND, Moto2Driver.GND
  SMoto1_EN: Part1.D2, Moto1Driver.EN
  SMoto1_Dir: Part1.D3, Moto1Driver.Dir
  SMoto1_Step: Part1.D4, Moto1Driver.Step
  DC_Moto_Ix2: Part1.D5
  SMoto2_Tx: Part1.D6, Moto2Driver.Tx
  SMoto2_Rx: Part1.D7, Moto2Driver.Rx
  SMoto1_CLK: Part1.D8, Moto1Driver.CLK
  DC_Moto_Ix1: Part1.D9
  SMoto2_Step: Part1.D10, Moto2Driver.Step
  SMoto2_CLK: Part1.D11/MOSI, Moto2Driver.CLK
  SMoto1_Tx: Part1.D12/MISO, Moto1Driver.Tx
  System_I2C_SCL: Part1.A5
  System_I2C_SDA: Part1.A4
  SMoto2_EN: Part1.A3, Moto2Driver.EN
  SMoto2_Dir: Part1.A2, Moto2Driver.Dir
  SMoto2Hall: Part1.A1
  SMoto1Hall: Part1.A0
  SMoto1_Rx: Part1.D13/SCK, Moto1Driver.Rx
  5V: Moto1Driver.VDD, Moto2Driver.VDD
  Moto1_B2: Moto1Driver.B2
  Moto1_B1: Moto1Driver.B1
  Moto1_A1: Moto1Driver.A1
  Moto1_A2: Moto1Driver.A2
  12V: Moto1Driver.VM, Moto2Driver.VM
  SMoto1_MS2: Moto1Driver.MS2
  SMoto1_MS1: Moto1Driver.MS1
  Moto2_B2: Moto2Driver.B2
  Moto2_B1: Moto2Driver.B1
  Moto2_A1: Moto2Driver.A1
  Moto2_A2: Moto2Driver.A2
  SMoto2_MS2: Moto2Driver.MS2
  SMoto2_MS1: Moto2Driver.MS1

notes:
  PWM: D11, D10, D9, D6, D5, D3

custom parts:
  TMC2209: TMC2209-LA stepper motor controller and driver. Supply voltage 4.75-28V Iphase up to 1.77A rms (2.5A peak)
